# Fritzing sketch breadboard_setup (saved by Fritzing 0.9.3b)
breadboards: 1

parts:
  IC1 = IC, DIP package, 16 pins [chip_label=MCP3008]
  Raspberry_Pi_1 = Raspberry Pi 3 [part_number=RPI-3-V1.2]
  R1 = Trimmer Potentiometer [maximum_resistance=10kΩ package=THT]

nets:
  N1: IC1.pin1, R1.wiper
  N2: IC1.pin9, IC1.pin14, Raspberry_Pi_1.GND, R1.leg2
  N3: IC1.pin10, Raspberry_Pi_1.GPIO8
  N4: IC1.pin11, Raspberry_Pi_1.GPIO10
  N5: IC1.pin12, Raspberry_Pi_1.GPIO9
  N6: IC1.pin13, Raspberry_Pi_1.GPIO11
  N7: IC1.pin15, IC1.pin16, Raspberry_Pi_1.5V, R1.leg1
